# Fritzing sketch SELF-BALANCING BICYCLE USING REACTING WHEEL WITH IMPROVING STABILITY (saved by Fritzing 0.9.3b)
circuit board: 8.46667cm x 5.64444cm

parts:
  Mod1 = Raspberry Pi Pico
  Part1 = HC-05 [part_number=HC-05 package="breakout board"]
  L298N1 = L298N DC motor driver
  M1 = Getriebemotor
  M2 = Getriebemotor
  U1 = LIPO-2000mAh [package=lipo-2000]
  GY1 = MPU-6050 Board GY-521 [form="♀ (female)" package=THT]
  S2 = SWITCH-DPDT-latching [package=os]

nets:
  N1: Mod1.pin_3, Mod1.pin_13, Mod1.pin_23, Mod1.pin_26, Mod1.pin_27, Mod1.pin_28, Mod1.pin_29, Mod1.pin_30, Mod1.pin_33, Mod1.pin_38, Mod1.pin_42, Part1.GND, L298N1.ENA, L298N1.IN2, L298N1.IN3, L298N1.IN4, GY1.pin2
  N2: Mod1.pin_4, GY1.pin4
  N3: Mod1.pin_5, GY1.pin3
  N4: Mod1.pin_21, Part1.RXD
  N5: Mod1.pin_22, Part1.TXD
  N6: Mod1.pin_24, L298N1.ENB
  N7: Mod1.pin_31, L298N1.IN1
  N8: Mod1.pin_39, Part1.VCC
  N9: Mod1.pin_40, S2.4
  N10: L298N1.OUT1, M2.pin_2
  N11: L298N1.OUT2, M2.pin_1
  N12: L298N1.OUT3, M1.pin_2
  N13: L298N1.OUT4, M1.pin_1
  N14: L298N1.12V, S2.1
  N15: L298N1.GND, U1.-
  N16: L298N1.5V, S2.6
  N17: U1.+, S2.3

custom parts:
  Raspberry Pi Pico: Raspberry Pi Pico. Based around the RP2040 microcontroller the Pico is a low cost microcontroller device bringing Raspberry Pi quality, cost, and easy of use to the microcontroller space. Jan 2021, Split part in to two versions: tht (this one) and SMD. This one will drill holes for a .1 in header in pcb to allow plugging in the module as well as providing pads to solder the module to the top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
  HC-05: A commonly available HC-05 Bluetooth breakout board.
  L298N DC motor driver: 2x DC motor driver with 78M05 positive voltage regulator (7..35 V) L298N: max 46 V, 2 A Set 5 V Enable jumper to enable 5 V regultor (needed for the L298N) and +5 V output at screw terminal or supply external +5 V at screw terminal Set ENA and/or ENB to +5 V to enable motor permanently or supply ENA and/or ENB with PWM signal IN1 and IN2 set rotation directory for motor A (OUT1/OUT2) IN2 and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
  MPU-6050 Board GY-521: Acelerometro y Giroscopio MPU-6050 Board GY-521
  SWITCH-DPDT-latching: DPDT latching pushbutton switch
